// Logisim project 4bitcraft.circ as structural Verilog: 1 circuit, main circuit main
module main (
);

  wire ADD, adder_1_cout, adder_1_out, adder_2_cout, adder_2_out, adder_3_cout, adder_3_out, adder_4_cout,
       adder_4_out, and_1_out, and_2_out, and_3_out, Carry, CLK, demultiplexer_2_out0, demultiplexer_2_out1,
       demultiplexer_2_out2, demultiplexer_2_out3, demultiplexer_3_out0, demultiplexer_3_out1,
       demultiplexer_3_out2, demultiplexer_3_out3, IACC, IALU, IMEM, IPC, JP, LD, LDI, nand_1_out,
       nand_2_out, nand_3_out, nand_4_out, NANDinst, not_1_out, or_1_out, ST, SUB, xor_1_out, xor_2_out,
       xor_3_out, xor_4_out, xor_5_out, xor_6_out, xor_7_out, xor_8_out, xor_9_out, XORinst;
  wire [1:0] InstructionCounter_q;
  wire [2:0] INST;
  wire [3:0] ACCdata, ALUdata, and_4_out, DATA, MEMdata, Microcode_data, ProgramCounter_q, PROMdata;

  Counter #(.max('h3), .trigger("falling"), .width(2)) InstructionCounter (
    .clr(and_1_out), .clk(CLK), .Q(InstructionCounter_q));  // open: load, up, count, D, carry
  and and_1 (and_1_out, IPC, not_1_out);
  not not_1 (not_1_out, CLK);
  Clock clock_1 (.out(CLK));
  Hex_Digit_Display #(.decimalPoint("false")) hex_digit_display_1 (.value(PROMdata));
  Hex_Digit_Display #(.decimalPoint("false")) hex_digit_display_2 (.value(ALUdata));
  Hex_Digit_Display #(.decimalPoint("false")) hex_digit_display_3 (.value(ACCdata));
  // Probe on {INST, InstructionCounter_q}
  ROM #(.addrWidth(5), .dataWidth(4)) Microcode (.addr({INST, InstructionCounter_q}), .data(Microcode_data));
  Hex_Digit_Display #(.decimalPoint("false")) hex_digit_display_4 (.value(MEMdata));
  Hex_Digit_Display #(.decimalPoint("false")) hex_digit_display_5 (.value(DATA));
  Counter #(.max('hf), .trigger("falling"), .width(4)) ProgramCounter (
    .load(and_2_out), .up(1'b1), .count(1'b1), .clk(IPC), .D(PROMdata), .Q(ProgramCounter_q));  // open: clr, carry
  and and_2 (and_2_out, JP, Carry);
  Multiplexer #(.select(2), .width(4)) multiplexer_1 (
    .in0(PROMdata), .in1(ALUdata), .in2(ACCdata), .in3(MEMdata), .out(DATA), .sel(Microcode_data[3:2]));
  and and_3 (and_3_out, Microcode_data[2], Microcode_data[3]);
  Demultiplexer #(.select(2)) demultiplexer_1 (
    .out0(IPC), .out1(IALU), .out2(IACC), .out3(IMEM), .in(CLK), .sel(Microcode_data[1:0]));
  Demultiplexer #(.select(2)) demultiplexer_2 (
    .out0(demultiplexer_2_out0), .out1(demultiplexer_2_out1), .out2(demultiplexer_2_out2),
    .out3(demultiplexer_2_out3), .in(1'b1), .sel(Microcode_data[3:2]));
  Demultiplexer #(.select(2)) demultiplexer_3 (
    .out0(demultiplexer_3_out0), .out1(demultiplexer_3_out1), .out2(demultiplexer_3_out2),
    .out3(demultiplexer_3_out3), .in(1'b1), .sel(Microcode_data[1:0]));
  ROM #(.addrWidth(4), .dataWidth(7)) ProgramROM (.addr(ProgramCounter_q), .data({INST, PROMdata}));
  LED OPRM (.in(demultiplexer_2_out0));
  LED u_IPC (.in(demultiplexer_3_out0));
  RAM #(.addrWidth(4), .dataWidth(4), .trigger("high"), .\type ("nonvolatile")) Memory (
    .addr(PROMdata), .we(IMEM), .oe(and_3_out), .din(ACCdata), .dout(MEMdata));
  LED OALU (.in(demultiplexer_2_out1));
  LED u_IALU (.in(demultiplexer_3_out1));
  LED OACC (.in(demultiplexer_2_out2));
  LED u_IACC (.in(demultiplexer_3_out2));
  LED OMEM (.in(demultiplexer_2_out3));
  LED u_IMEM (.in(demultiplexer_3_out3));
  Demultiplexer #(.select(3)) demultiplexer_4 (
    .out0(LDI), .out1(LD), .out2(ST), .out3(JP), .out4(ADD), .out5(SUB), .out6(NANDinst), .out7(XORinst),
    .in(1'b1), .sel(INST));
  xor xor_1 (xor_1_out, DATA[0], SUB);
  xor xor_2 (xor_2_out, DATA[1], SUB);
  xor xor_3 (xor_3_out, DATA[2], SUB);
  xor xor_4 (xor_4_out, DATA[3], SUB);
  Register #(.width(4)) Accumulator (.D(DATA), .en(IACC), .clk(IACC), .Q(ACCdata));  // open: clr
  xor xor_5 (xor_5_out, SUB, Carry);
  Adder #(.width(1)) adder_1 (.a(ACCdata[0]), .b(xor_1_out), .out(adder_1_out), .cin(xor_5_out), .cout(adder_1_cout));
  Adder #(.width(1)) adder_2 (
    .a(ACCdata[1]), .b(xor_2_out), .out(adder_2_out), .cin(adder_1_cout), .cout(adder_2_cout));
  Adder #(.width(1)) adder_3 (
    .a(ACCdata[2]), .b(xor_3_out), .out(adder_3_out), .cin(adder_2_cout), .cout(adder_3_cout));
  Adder #(.width(1)) adder_4 (
    .a(ACCdata[3]), .b(xor_4_out), .out(adder_4_out), .cin(adder_3_cout), .cout(adder_4_cout));
  D_Flip_Flop #(.trigger("falling")) u_Carry (.D(adder_4_cout), .clk(or_1_out), .Q(Carry));  // open: Qn, preset, reset
  or or_1 (or_1_out, SUB, ADD);
  and and_4 (and_4_out[0], or_1_out, adder_1_out);
  and and_5 (and_4_out[1], or_1_out, adder_2_out);
  and and_6 (and_4_out[2], or_1_out, adder_3_out);
  and and_7 (and_4_out[3], or_1_out, adder_4_out);
  and and_8 (and_4_out[0], NANDinst, nand_1_out);
  nand nand_1 (nand_1_out, ACCdata[0], DATA[0]);
  and and_9 (and_4_out[1], NANDinst, nand_2_out);
  nand nand_2 (nand_2_out, ACCdata[1], DATA[1]);
  and and_10 (and_4_out[2], NANDinst, nand_3_out);
  nand nand_3 (nand_3_out, ACCdata[2], DATA[2]);
  and and_11 (and_4_out[3], NANDinst, nand_4_out);
  nand nand_4 (nand_4_out, ACCdata[3], DATA[3]);
  and and_12 (and_4_out[0], XORinst, xor_6_out);
  xor xor_6 (xor_6_out, ACCdata[0], DATA[0]);
  and and_13 (and_4_out[1], XORinst, xor_7_out);
  xor xor_7 (xor_7_out, ACCdata[1], DATA[1]);
  and and_14 (and_4_out[2], XORinst, xor_8_out);
  xor xor_8 (xor_8_out, ACCdata[2], DATA[2]);
  and and_15 (and_4_out[3], XORinst, xor_9_out);
  xor xor_9 (xor_9_out, ACCdata[3], DATA[3]);
  Pull_Resistor pull_resistor_1 (.node(and_4_out));
  Register #(.width(4)) ALU (.D(and_4_out), .en(IALU), .clk(IALU), .Q(ALUdata));  // open: clr

  // Notes on the sheet:
  //   contents of Microcode (hex, n*v repeats v):
  //   2 4 9 9 e 4 9 9 b 4 9 9 4 9 9 9 d 6 4 9 d 6 4 9 1 6 4 9 1 6 4 9
  //   contents of ProgramROM (hex, n*v repeats v):
  //   f 2f 3 20 1 21 4e 10 41 20 1f 4f 34
  //   and_4 drives only 1 and floats otherwise
  //   and_5 drives only 1 and floats otherwise
  //   and_6 drives only 1 and floats otherwise
  //   and_7 drives only 1 and floats otherwise
  //   and_8 drives only 1 and floats otherwise
  //   and_9 drives only 1 and floats otherwise
  //   and_10 drives only 1 and floats otherwise
  //   and_11 drives only 1 and floats otherwise
  //   and_12 drives only 1 and floats otherwise
  //   and_13 drives only 1 and floats otherwise
  //   and_14 drives only 1 and floats otherwise
  //   and_15 drives only 1 and floats otherwise
endmodule
